# Fritzing sketch Control_circut (saved by Fritzing 0.9.1b)
circuit board: 5.09641cm x 4.29838cm
breadboards: 1

parts:
  Power_plug1 = Power plug
  U1 = atmega328 [package=dip]
  JP1 = FTDI_BASIC [package=ftdi_basic]
  J2 = shrouded pin header, 10 pins [form="♂ (shrouded male)"]
  U2 = Voltage Regulator - 5V [package="TO220 [THT]"]
  U3 = XBee

nets (from the pcb view):
  GND: Power_plug1.GND, U1.GND#7, J2.pin2, U2.GND, U3.GND
  N1: Power_plug1.VCC, U2.input_voltage
  N2: U1.D0_(RX), JP1.2
  N3: U1.D1_(TX), JP1.1
  N4: U1.D2, J2.pin9
  N5: U1.D4, J2.pin10
  VCC: U1.VCC, J2.pin1, U2.output_voltage, U3.VCC
  N6: U1.A0, J2.pin3
  N7: U1.A1, J2.pin4
  N8: U1.A2, J2.pin5
  N9: U1.A3, J2.pin6
  N10: U1.A4, J2.pin7
  N11: U1.A5, J2.pin8
