# Fritzing sketch control_circuit_2 (saved by Fritzing 0.9.1b)
circuit board: 6.29176cm x 4.55698cm
breadboards: 1

parts:
  Part1 = Arduino Nano (Rev3.0)
  J1 = Power Jack [package=power_jack_pth_lock]
  JP1 = FTDI_BASIC [package=ftdi_basic]
  U1 = XBee

nets:
  N1: Part1.D1/TX, U1.pin3
  N2: Part1.D0/RX, U1.pin2
  N3: Part1.D2, U1.pin9
  N4: Part1.D4, JP1.5
  N5: Part1.D6, JP1.1
  N6: Part1.D7, JP1.6
  N7: Part1.D8, JP1.2
  N8: Part1.D9, JP1.3
  N9: Part1.D10, JP1.4
  N10: Part1.VIN, J1.PWR
  GND: Part1.GND, J1.GND
